// Digital circuit P1_Multiplexor.dig as structural Verilog
module P1_Multiplexor (
  input  S1,
  input  S2,
  input  S3,
  input  A,
  input  B,
  input  C,
  input  D,
  input  E,
  input  F,
  input  G,
  input  H,
  output OUT
);

  wire and_1_out, and_2_out, and_3_out, and_4_out, and_5_out, and_6_out, and_7_out, and_8_out, not_1_out,
       not_2_out, not_3_out, or_1_out, or_2_out;

  not not_1 (not_1_out, S1);
  not not_2 (not_2_out, S2);
  not not_3 (not_3_out, S3);
  and and_1 (and_1_out, A, not_1_out, not_2_out, not_3_out);
  and and_2 (and_2_out, B, S3, not_2_out, not_1_out);
  and and_3 (and_3_out, C, S2, not_1_out, not_3_out);
  and and_4 (and_4_out, D, not_1_out, S2, S3);
  and and_5 (and_5_out, E, S1, not_2_out, not_3_out);
  and and_6 (and_6_out, F, S1, S3, not_2_out);
  and and_7 (and_7_out, G, S1, S2, not_3_out);
  and and_8 (and_8_out, H, S1, S2, S3);
  or or_1 (or_1_out, and_1_out, and_2_out, and_3_out, and_4_out);
  or or_2 (or_2_out, and_5_out, and_6_out, and_7_out, and_8_out);
  or or_3 (OUT, or_1_out, or_2_out);
endmodule
