// Digital circuit P2_Demultiplexor.dig as structural Verilog
module P2_Demultiplexor (
  input  S1,
  input  S2,
  input  IN,
  output A,
  output B,
  output C,
  output D
);

  wire not_1_out, not_2_out;

  not not_1 (not_1_out, S1);
  not not_2 (not_2_out, S2);
  and and_1 (A, IN, not_1_out, not_2_out);
  and and_2 (B, IN, not_1_out, S2);
  and and_3 (C, IN, not_2_out, S1);
  and and_4 (D, IN, S1, S2);
endmodule
