// Digital circuit P3a_FFRS.dig as structural Verilog
module P3a_FFRS (
  input  S,
  input  R,
  input  C,
  output Q
);

  wire nand_1_out, nand_2_out, nand_3_out, nand_4_out, nand_5_out, nand_6_out, nand_8_out, not_1_out;

  nand nand_1 (nand_1_out, S, C);
  nand nand_2 (nand_2_out, C, R);
  not not_1 (not_1_out, C);
  nand nand_3 (nand_3_out, nand_1_out, nand_4_out);
  nand nand_4 (nand_4_out, nand_3_out, nand_2_out);
  nand nand_5 (nand_5_out, nand_3_out, not_1_out);
  nand nand_6 (nand_6_out, not_1_out, nand_4_out);
  nand nand_7 (Q, nand_5_out, nand_8_out);
  nand nand_8 (nand_8_out, Q, nand_6_out);

  // Notes on the sheet:
  //   Un Flip-Flop RS está compuesto por dos latch concatenados uno delante del otro.
  //   Cuando el clock vale 1, la parte A está activa mientras que la B no recibe información.
  //   En el momento en el que cambia de 1 a 0, la información que había en A "pasa" a B.
  //   Cuando A está activo, B está inactivo gracias al elemento inversor conectado al clock.
  //   A
  //   B
endmodule
