// Digital circuit P3b_FFJK.dig as structural Verilog
module P3b_FFJK (
  input  S,
  input  R,
  input  C,
  output Q
);

  wire and_1_out, and_2_out, nand_1_out, nand_2_out, nand_3_out, nand_4_out, nand_5_out, nand_6_out,
       nand_8_out, not_1_out;

  and and_1 (and_1_out, S, nand_8_out);
  and and_2 (and_2_out, Q, R);
  not not_1 (not_1_out, C);
  nand nand_1 (nand_1_out, and_1_out, C);
  nand nand_2 (nand_2_out, C, and_2_out);
  nand nand_3 (nand_3_out, nand_1_out, nand_4_out);
  nand nand_4 (nand_4_out, nand_3_out, nand_2_out);
  nand nand_5 (nand_5_out, nand_3_out, not_1_out);
  nand nand_6 (nand_6_out, not_1_out, nand_4_out);
  nand nand_7 (Q, nand_5_out, nand_8_out);
  nand nand_8 (nand_8_out, Q, nand_6_out);

  // Notes on the sheet:
  //   En el Flip-Flop RS presenta un estado de indeterminación cuando ambos pines, de Reset y Set se actival almismo tiempo.
  //   Dicho estado de indeterminación se puede presentar para configuraciones 1-1 o 0-0 según esté compuesta por compuertas 
  //   NAND o compuertas NOR.
  //   El Flip-Flop JK es básicamente un RS (Maestro-Esclavo) con la particularidad de que para corregir la indeterminación no deseada 
  //   se retroalimentan las salidas del Flip-Flop, cambiando nuevamente el estado final.
endmodule
