// Digital circuit P4_PIN.dig as structural Verilog
module P4_PIN (
  input  Set,
  input  Enable,
  input  Clock,
  input  Clear,
  input  Set_2,
  input  Enable_2,
  input  Clock_2,
  input  Clear_2,
  input  PIN_1,
  input  PIN_2,
  input  PIN_3,
  input  PIN_4,
  input  in_17,
  input  in_18,
  input  in_19,
  input  in_20,
  input  Set_3,
  input  Enable_3,
  input  Clock_3,
  input  Clear_3,
  input  D1,
  input  D2,
  input  D3,
  input  D4,
  output out_5,
  output out_6,
  output out_7,
  output out_8,
  output out_29,
  output out_30,
  output out_31,
  output out_32,
  output out_33,
  output out_34,
  output out_35,
  output out_36
);

  wire d_ff_as_3_q, d_ff_as_6_q, d_ff_as_9_q, d_ff_as_12_q, driver_1_out, driver_2_out, driver_3_out,
       driver_4_out, multiplexer_1_out, multiplexer_2_out, multiplexer_3_out, multiplexer_4_out,
       multiplexer_5_out, multiplexer_6_out, multiplexer_7_out, multiplexer_8_out, multiplexer_9_out,
       multiplexer_10_out, multiplexer_11_out, multiplexer_12_out;

  Multiplexer multiplexer_1 (.sel(Enable_2), .in_0(out_33), .in_1(PIN_1), .out(multiplexer_1_out));
  Multiplexer multiplexer_2 (.sel(Enable), .in_0(out_5), .in_1(driver_1_out), .out(multiplexer_2_out));
  Multiplexer multiplexer_3 (.sel(Enable_3), .in_0(d_ff_as_3_q), .in_1(D1), .out(multiplexer_3_out));
  assign driver_1_out = out_33 ? in_17 : 1'bz;  // Driver driver_1
  D_FF_AS d_ff_as_1 (.Set(Set_2), .D(multiplexer_1_out), .C(Clock_2), .Clr(Clear_2), .Q(out_33));  // open: nQ
  D_FF_AS d_ff_as_2 (.Set(Set), .D(multiplexer_2_out), .C(Clock), .Clr(Clear), .Q(out_5));  // open: nQ
  D_FF_AS d_ff_as_3 (.Set(Set_3), .D(multiplexer_3_out), .C(Clock_3), .Clr(Clear_3), .Q(d_ff_as_3_q));  // open: nQ
  assign out_29 = ~out_33 ? d_ff_as_3_q : 1'bz;  // DriverInvSel driverinvsel_1
  Multiplexer multiplexer_4 (.sel(Enable_2), .in_0(out_34), .in_1(PIN_2), .out(multiplexer_4_out));
  assign driver_2_out = out_34 ? in_18 : 1'bz;  // Driver driver_2
  Multiplexer multiplexer_5 (.sel(Enable), .in_0(out_6), .in_1(driver_2_out), .out(multiplexer_5_out));
  Multiplexer multiplexer_6 (.sel(Enable_3), .in_0(d_ff_as_6_q), .in_1(D2), .out(multiplexer_6_out));
  D_FF_AS d_ff_as_4 (.Set(Set_2), .D(multiplexer_4_out), .C(Clock_2), .Clr(Clear_2), .Q(out_34));  // open: nQ
  D_FF_AS d_ff_as_5 (.Set(Set), .D(multiplexer_5_out), .C(Clock), .Clr(Clear), .Q(out_6));  // open: nQ
  D_FF_AS d_ff_as_6 (.Set(Set_3), .D(multiplexer_6_out), .C(Clock_3), .Clr(Clear_3), .Q(d_ff_as_6_q));  // open: nQ
  assign out_30 = ~out_34 ? d_ff_as_6_q : 1'bz;  // DriverInvSel driverinvsel_2
  Multiplexer multiplexer_7 (.sel(Enable_2), .in_0(out_35), .in_1(PIN_3), .out(multiplexer_7_out));
  Multiplexer multiplexer_8 (.sel(Enable), .in_0(out_7), .in_1(driver_3_out), .out(multiplexer_8_out));
  Multiplexer multiplexer_9 (.sel(Enable_3), .in_0(d_ff_as_9_q), .in_1(D3), .out(multiplexer_9_out));
  assign driver_3_out = out_35 ? in_19 : 1'bz;  // Driver driver_3
  D_FF_AS d_ff_as_7 (.Set(Set_2), .D(multiplexer_7_out), .C(Clock_2), .Clr(Clear_2), .Q(out_35));  // open: nQ
  D_FF_AS d_ff_as_8 (.Set(Set), .D(multiplexer_8_out), .C(Clock), .Clr(Clear), .Q(out_7));  // open: nQ
  D_FF_AS d_ff_as_9 (.Set(Set_3), .D(multiplexer_9_out), .C(Clock_3), .Clr(Clear_3), .Q(d_ff_as_9_q));  // open: nQ
  assign out_31 = ~out_35 ? d_ff_as_9_q : 1'bz;  // DriverInvSel driverinvsel_3
  Multiplexer multiplexer_10 (.sel(Enable_2), .in_0(out_36), .in_1(PIN_4), .out(multiplexer_10_out));
  assign driver_4_out = out_36 ? in_20 : 1'bz;  // Driver driver_4
  Multiplexer multiplexer_11 (.sel(Enable), .in_0(out_8), .in_1(driver_4_out), .out(multiplexer_11_out));
  Multiplexer multiplexer_12 (.sel(Enable_3), .in_0(d_ff_as_12_q), .in_1(D4), .out(multiplexer_12_out));
  D_FF_AS d_ff_as_10 (.Set(Set_2), .D(multiplexer_10_out), .C(Clock_2), .Clr(Clear_2), .Q(out_36));  // open: nQ
  D_FF_AS d_ff_as_11 (.Set(Set), .D(multiplexer_11_out), .C(Clock), .Clr(Clear), .Q(out_8));  // open: nQ
  D_FF_AS d_ff_as_12 (.Set(Set_3), .D(multiplexer_12_out), .C(Clock_3), .Clr(Clear_3), .Q(d_ff_as_12_q));  // open: nQ
  assign out_32 = ~out_36 ? d_ff_as_12_q : 1'bz;  // DriverInvSel driverinvsel_4

  // Other names for the same wires on the sheet: A1 = in_17; A2 = in_18; A3 = in_19; A4 = in_20; B1 = out_33;
  //   B2 = out_34; B3 = out_35; B4 = out_36

  // Notes on the sheet:
  //   Registro Configuración: Este registro es el que "Elegirá" si el PIN a usar será usado como entrada o como salida, para esta configuración se tiene que será de entrada siempre que la salida correspondiente sea igual a 1
  //   y será de salida siempre que las "Q" (salidas del registro) correspondientes sean iguales a 0.
  //   Registro Memoria: Cuando el registro de configuración tiene un valor de 1, se le está indicando al PIN que será un pin de entrada, por lo cual los datos que entran al circuito mediante las entradas denotadas por las letras A serán transferidos a este circuito de registro
  //   y será almacenado en la memoria.
  //   Registro Control: Mediante el uso de los Buffers puede notarse que si está activado el Registro Memoria, significa que el Registro Control está desactivado y viceversa.
  //   El registro control será activado entonces cuando la salida del Registro configuración sea igual a cero, como se dijo anteriormente, si la salida de la configuración es igual a 0, significa que el PIN será un pin de salida de datos.
  //   Configuración
  //   Memoria
  //   Control
endmodule
